// Logisim project processador.circ as structural Verilog
module banco_de_registradores (
  input  [3:0] RD,
  input  [3:0] Resultado,
  input  [3:0] RG1,
  input  [3:0] RG2,
  output [3:0] ULA_A,
  output [3:0] ULA_B
);

  wire decoder_1_out0, decoder_1_out1, decoder_1_out2, decoder_1_out3, decoder_1_out4, decoder_1_out5,
       decoder_1_out6, decoder_1_out7, decoder_1_out8, decoder_1_out9, decoder_1_out10, decoder_1_out11,
       decoder_1_out12, decoder_1_out13, decoder_1_out14, decoder_1_out15;
  wire [3:0] registradores_1_r0, registradores_1_r1, registradores_1_r2, registradores_1_r3,
       registradores_1_r4, registradores_1_r5, registradores_1_r6, registradores_1_r7, registradores_1_r8,
       registradores_1_r9, registradores_1_r10, registradores_1_r11, registradores_1_r12,
       registradores_1_r13, registradores_1_r14, registradores_1_r15;

  Decoder #(.select(4)) decoder_1 (
    .out0(decoder_1_out0), .out1(decoder_1_out1), .out2(decoder_1_out2), .out3(decoder_1_out3),
    .out4(decoder_1_out4), .out5(decoder_1_out5), .out6(decoder_1_out6), .out7(decoder_1_out7),
    .out8(decoder_1_out8), .out9(decoder_1_out9), .out10(decoder_1_out10), .out11(decoder_1_out11),
    .out12(decoder_1_out12), .out13(decoder_1_out13), .out14(decoder_1_out14), .out15(decoder_1_out15),
    .sel(RD));  // open: en
  registradores registradores_1 (
    .Resultado(Resultado), .en1(decoder_1_out0), .en2(decoder_1_out1), .en3(decoder_1_out2),
    .en4(decoder_1_out3), .e5(decoder_1_out4), .en6(decoder_1_out5), .en7(decoder_1_out6),
    .en8(decoder_1_out7), .en9(decoder_1_out8), .en10(decoder_1_out9), .en11(decoder_1_out10),
    .en12(decoder_1_out11), .en13(decoder_1_out12), .en14(decoder_1_out13), .en15(decoder_1_out14),
    .en16(decoder_1_out15), .R0(registradores_1_r0), .R1(registradores_1_r1), .R2(registradores_1_r2),
    .R3(registradores_1_r3), .R4(registradores_1_r4), .R5(registradores_1_r5), .R6(registradores_1_r6),
    .R7(registradores_1_r7), .R8(registradores_1_r8), .R9(registradores_1_r9), .R10(registradores_1_r10),
    .R11(registradores_1_r11), .R12(registradores_1_r12), .R13(registradores_1_r13),
    .R14(registradores_1_r14), .R15(registradores_1_r15));
  Multiplexer #(.select(4), .width(4)) multiplexer_1 (
    .in0(registradores_1_r0), .in1(registradores_1_r1), .in2(registradores_1_r2), .in3(registradores_1_r3),
    .in4(registradores_1_r4), .in5(registradores_1_r5), .in6(registradores_1_r6), .in7(registradores_1_r7),
    .in8(registradores_1_r8), .in9(registradores_1_r9), .in10(registradores_1_r10),
    .in11(registradores_1_r11), .in12(registradores_1_r12), .in13(registradores_1_r13),
    .in14(registradores_1_r14), .in15(registradores_1_r15), .out(ULA_A), .sel(RG1));  // open: en
  Multiplexer #(.select(4), .width(4)) multiplexer_2 (
    .in0(registradores_1_r0), .in1(registradores_1_r1), .in2(registradores_1_r2), .in3(registradores_1_r3),
    .in4(registradores_1_r4), .in5(registradores_1_r5), .in6(registradores_1_r6), .in7(registradores_1_r7),
    .in8(registradores_1_r8), .in9(registradores_1_r9), .in10(registradores_1_r10),
    .in11(registradores_1_r11), .in12(registradores_1_r12), .in13(registradores_1_r13),
    .in14(registradores_1_r14), .in15(registradores_1_r15), .out(ULA_B), .sel(RG2));  // open: en
endmodule

module registradores (
  input  [3:0] Resultado,
  input  en1,
  input  en2,
  input  en3,
  input  en4,
  input  e5,
  input  en6,
  input  en7,
  input  en8,
  input  en9,
  input  en10,
  input  en11,
  input  en12,
  input  en13,
  input  en14,
  input  en15,
  input  en16,
  output [3:0] R0,
  output [3:0] R1,
  output [3:0] R2,
  output [3:0] R3,
  output [3:0] R4,
  output [3:0] R5,
  output [3:0] R6,
  output [3:0] R7,
  output [3:0] R8,
  output [3:0] R9,
  output [3:0] R10,
  output [3:0] R11,
  output [3:0] R12,
  output [3:0] R13,
  output [3:0] R14,
  output [3:0] R15
);

  Register #(.width(4)) u_R0 (.D(Resultado), .en(en1), .Q(R0));  // open: clk, clr
  Register #(.width(4)) u_R1 (.D(Resultado), .en(en2), .Q(R1));  // open: clk, clr
  Register #(.width(4)) u_R2 (.D(Resultado), .en(en3), .Q(R2));  // open: clk, clr
  Register #(.width(4)) u_R3 (.D(Resultado), .en(en4), .Q(R3));  // open: clk, clr
  Register #(.width(4)) u_R4 (.D(Resultado), .en(e5), .Q(R4));  // open: clk, clr
  Register #(.width(4)) u_R5 (.D(Resultado), .en(en6), .Q(R5));  // open: clk, clr
  Register #(.width(4)) u_R6 (.D(Resultado), .en(en7), .Q(R6));  // open: clk, clr
  Register #(.width(4)) u_R7 (.D(Resultado), .en(en8), .Q(R7));  // open: clk, clr
  Register #(.width(4)) u_R8 (.D(Resultado), .en(en9), .Q(R8));  // open: clk, clr
  Register #(.width(4)) u_R9 (.D(Resultado), .en(en10), .Q(R9));  // open: clk, clr
  Register #(.width(4)) u_R10 (.D(Resultado), .en(en11), .Q(R10));  // open: clk, clr
  Register #(.width(4)) u_R11 (.D(Resultado), .en(en12), .Q(R11));  // open: clk, clr
  Register #(.width(4)) u_R12 (.D(Resultado), .en(en13), .Q(R12));  // open: clk, clr
  Register #(.width(4)) u_R13 (.D(Resultado), .en(en14), .Q(R13));  // open: clk, clr
  Register #(.width(4)) u_R14 (.D(Resultado), .en(en15), .Q(R14));  // open: clk, clr
  Register #(.width(4)) u_R15 (.D(Resultado), .en(en16), .Q(R15));  // open: clk, clr
endmodule

module ULA (
  input  [3:0] A,
  input  [3:0] B,
  input  in_3,
  input  S2,
  input  S1,
  input  S0,
  output [3:0] SAIDA,
  output C_out,
  output OVERFLOW
);

  wire ula_celula_1bit_1_c_out, ula_celula_1bit_2_c_out, ula_celula_1bit_3_c_out, ula_celula_1bit_4_c_out;

  ULA_celula_1bit ula_celula_1bit_1 (
    .A(A[3]), .B(B[3]), .C_in(ula_celula_1bit_2_c_out), .OUT_RESULT(SAIDA[3]), .SEL_OP({S2, S1, S0}),
    .C_out(ula_celula_1bit_1_c_out));
  overflow overflow_1 (
    .A(A[3]), .B(B[3]), .S(SAIDA[3]), .C_IN(ula_celula_1bit_1_c_out), .SELETOR({S2, S1, S0}),
    .OVERFLOW(OVERFLOW));
  ULA_celula_1bit ula_celula_1bit_2 (
    .A(A[2]), .B(B[2]), .C_in(ula_celula_1bit_3_c_out), .OUT_RESULT(SAIDA[2]), .SEL_OP({S2, S1, S0}),
    .C_out(ula_celula_1bit_2_c_out));
  ULA_celula_1bit ula_celula_1bit_3 (
    .A(A[1]), .B(B[1]), .C_in(ula_celula_1bit_4_c_out), .OUT_RESULT(SAIDA[1]), .SEL_OP({S2, S1, S0}),
    .C_out(ula_celula_1bit_3_c_out));
  ULA_celula_1bit ula_celula_1bit_4 (
    .A(A[0]), .B(B[0]), .C_in(in_3), .OUT_RESULT(SAIDA[0]), .SEL_OP({S2, S1, S0}),
    .C_out(ula_celula_1bit_4_c_out));
  and AND (C_out, ula_celula_1bit_1_c_out, ~S2);  // AND_Gate

  // Notes on the sheet:
  //   S2    S1   S0
  //   0      0      0        CLEAR  
  //   0      0      1          NAND
  //   0      1      0          A  - B
  //   0      1      1          A + B
  //   1      0      0         A xor B 
  //   1      0      1         A or B
  //   1      1      0        A and B
  //   1      1      1       PRESET
  //   Tabela de Operaçoes
  //   OPERAÇAO
endmodule

module ULA_celula_1bit (
  input  A,
  input  B,
  input  C_in,
  input  [2:0] SEL_OP,
  output OUT_RESULT,
  output C_out
);

  wire adder_1_cout, adder_1_out, AND_2_out, AND_out, clear_1_out_3, NAND_out, OR_out, preset_1_out_3,
       subtractor_1_bout, subtractor_1_out, XOR_out;

  clear clear_1 (.in_1(A), .in_2(B), .out_3(clear_1_out_3));
  nand NAND (NAND_out, A, B);
  Adder #(.width(1)) adder_1 (.a(A), .b(B), .out(adder_1_out), .cin(C_in), .cout(adder_1_cout));
  Subtractor #(.width(1)) subtractor_1 (.a(A), .b(B), .out(subtractor_1_out), .bin(C_in), .bout(subtractor_1_bout));
  xor XOR (XOR_out, A, B);
  or OR (OR_out, A, B);
  and AND (AND_out, A, B);
  preset preset_1 (.in_1(A), .in_2(B), .out_3(preset_1_out_3));
  Multiplexer #(.select(3), .enable("false")) multiplexer_1 (
    .in0(clear_1_out_3), .in1(NAND_out), .in2(adder_1_out), .in3(subtractor_1_out), .in4(XOR_out),
    .in5(OR_out), .in6(AND_out), .in7(preset_1_out_3), .out(OUT_RESULT), .sel(SEL_OP));
  and AND_2 (AND_2_out, ~SEL_OP[2], SEL_OP[1], ~SEL_OP[0]);  // AND_Gate
  Multiplexer #(.enable("false")) multiplexer_2 (
    .in0(adder_1_cout), .in1(subtractor_1_bout), .out(C_out), .sel(AND_2_out));
endmodule

module preset (
  input  in_1,
  input  in_2,
  output out_3
);


  assign out_3 = 1'b1;
endmodule

module clear (
  input  in_1,
  input  in_2,
  output out_3
);


  assign out_3 = 1'b0;
endmodule

module overflow (
  input  A,
  input  B,
  input  S,
  input  C_IN,
  input  [2:0] SELETOR,
  output OVERFLOW
);

  wire AND_2_out, AND_3_out, AND_out, OR_out;

  and AND (AND_out, SELETOR[0], SELETOR[1]);  // AND_Gate
  and AND_2 (AND_2_out, ~A, S, ~B);  // AND_Gate
  and AND_3 (AND_3_out, A, ~S, B);  // AND_Gate
  or OR (OR_out, AND_2_out, AND_3_out);
  Multiplexer #(.enable("false")) multiplexer_1 (.in0(OR_out), .in1(C_IN), .out(OVERFLOW), .sel(AND_out));
endmodule

module \ROM__instruções  (
  input  [3:0] in_1,
  output [7:0] UC
);

  ROM #(.addrWidth(4)) rom_1 (.addr(in_1), .data(UC));  // open: sel
endmodule
